// Logisim project arch.circ as structural Verilog
module CONTROL (
  input  [2:0] RING_IN,
  input  [3:0] OPCODE,
  output INC_PC,
  output EN_PC,
  output LD_AR,
  output EN_AR,
  output EN_RAM,
  output LD_IR,
  output EN_IR,
  output SET_ACK,
  output LD_ACC,
  output EN_ACC,
  output LD_OUT,
  output LD_TMP,
  output EN_ALU,
  output EN_SUB
);

  wire ADD, and_1_out, and_2_out, and_3_out, and_4_out, CYC4, CYC5, decoder_1_out6, decoder_1_out7, HLT, LDA,
       or_2_out, or_3_out, or_4_out, or_5_out, OUT_C, SUB;

  Decoder #(.select(3)) decoder_1 (
    .out1(EN_PC), .out2(INC_PC), .out3(EN_IR), .out4(CYC4), .out5(CYC5), .out6(decoder_1_out6),
    .out7(decoder_1_out7), .sel(RING_IN));  // open: out0, en
  Decoder #(.select(4)) decoder_2 (
    .out0(LDA), .out1(ADD), .out2(SUB), .out14(OUT_C), .out15(HLT), .sel(OPCODE));  // open: out3, out4, out5, out6, out7, out8, out9, out10, out11, out12, out13, en
  or or_1 (LD_AR, EN_PC, EN_IR);
  or or_2 (or_2_out, LDA, ADD, SUB);
  and and_1 (and_1_out, or_2_out, CYC4);
  or or_3 (or_3_out, LDA, OUT_C);
  or or_4 (or_4_out, ADD, SUB);
  or or_5 (or_5_out, ADD, SUB);
  or or_6 (EN_AR, INC_PC, and_1_out);
  and and_2 (and_2_out, or_3_out, CYC4);
  and and_3 (and_3_out, CYC5, or_4_out);
  and and_4 (and_4_out, LDA, CYC4);
  and and_5 (EN_ALU, CYC5, or_5_out);
  and and_6 (EN_SUB, CYC5, SUB);
  or or_7 (SET_ACK, and_2_out, and_3_out);
  or or_8 (LD_ACC, and_4_out, EN_ALU);
  and and_7 (EN_ACC, CYC4, OUT_C);
  and and_8 (LD_TMP, CYC4, or_5_out);

  assign EN_RAM = EN_AR;
  assign LD_IR = INC_PC;
  assign LD_OUT = EN_ACC;

  // Other names for the same wires on the sheet: CYC1 = EN_PC; CYC2 = INC_PC; CYC3 = EN_IR
endmodule

module RING (
  input  CLK,
  input  CLR,
  output [2:0] RING_OUT
);

  wire and_1_out, not_1_out;
  wire [2:0] multiplexer_1_out;

  Multiplexer #(.width(3)) multiplexer_1 (.in1(3'b001), .out(multiplexer_1_out), .sel(and_1_out));  // open: in0
  Counter #(.max('h5), .width(3)) counter_1 (
    .load(and_1_out), .D(multiplexer_1_out), .Q(RING_OUT), .clk(CLK), .clr(CLR));  // open: count, carry, up
  not not_1 (not_1_out, RING_OUT[1]);
  and and_1 (and_1_out, RING_OUT[0], not_1_out, RING_OUT[2]);
endmodule

module ACC (
  input  [7:0] ACC_IN,
  input  LD_ACC,
  input  EN_ACC,
  input  CLK_N,
  output [7:0] ACC_OUT
);

  wire [7:0] multiplexer_1_out, register_1_q;

  Multiplexer #(.width(8)) multiplexer_1 (.in0(register_1_q), .in1(ACC_IN), .out(multiplexer_1_out), .sel(LD_ACC));
  Register #(.trigger("falling")) register_1 (.D(multiplexer_1_out), .Q(register_1_q), .clk(CLK_N));  // open: en, clr
  assign ACC_OUT = EN_ACC ? register_1_q : 8'bz;  // Controlled_Buffer controlled_buffer_1
endmodule

module RAM8x8 (
  input  EN_RAM,
  input  [2:0] ADDR_IN,
  output [7:0] RAM_OUT
);

  wire [7:0] ram_1_dout;

  RAM #(.addrWidth(3), .enables("line"), .\type ("nonvolatile")) ram_1 (
    .addr(ADDR_IN), .dout(ram_1_dout));  // open: we, clk, din
  assign RAM_OUT = EN_RAM ? ram_1_dout : 8'bz;  // Controlled_Buffer controlled_buffer_1
endmodule

module NEURON (
  output out_1,
  output out_2,
  output out_3,
  output out_4,
  output out_5
);

  wire clock_1_out, control_1_en_acc, control_1_en_ar, control_1_en_ir, control_1_en_pc, control_1_en_ram,
       control_1_inc_pc, control_1_ld_acc, control_1_ld_ar, control_1_ld_ir, not_1_out;
  wire [2:0] ar_1_ar_out, ring_1_ring_out;
  wire [3:0] OPCODE;
  wire [3:3] ir_1_addr_out;
  wire [7:0] WBUS;

  Clock clock_1 (.out(clock_1_out));
  not not_1 (not_1_out, clock_1_out);
  RING ring_1 (.CLK(clock_1_out), .RING_OUT(ring_1_ring_out));  // open: CLR
  CONTROL control_1 (
    .RING_IN(ring_1_ring_out), .OPCODE(OPCODE), .INC_PC(control_1_inc_pc), .EN_PC(control_1_en_pc),
    .LD_AR(control_1_ld_ar), .EN_AR(control_1_en_ar), .EN_RAM(control_1_en_ram), .LD_IR(control_1_ld_ir),
    .EN_IR(control_1_en_ir), .SET_ACK(out_1), .LD_ACC(control_1_ld_acc), .EN_ACC(control_1_en_acc),
    .LD_OUT(out_2), .LD_TMP(out_3), .EN_ALU(out_4), .EN_SUB(out_5));
  PC pc_1 (.EN_PC(control_1_en_pc), .INC_PC(control_1_inc_pc), .CLK(clock_1_out), .PC_OUT(WBUS[2:0]));  // open: CLR
  AR ar_1 (.LD_AR(control_1_ld_ar), .EN_AR(control_1_en_ar), .CLK_N(not_1_out), .AR_OUT(ar_1_ar_out));  // open: AR_IN
  RAM8x8 ram8x8_1 (.EN_RAM(control_1_en_ram), .ADDR_IN(ar_1_ar_out), .RAM_OUT(WBUS));
  ACC acc_1 (.ACC_IN(WBUS), .LD_ACC(control_1_ld_acc), .EN_ACC(control_1_en_acc), .CLK_N(not_1_out), .ACC_OUT(WBUS));
  IR ir_1 (
    .IR_IN(WBUS), .LD_IR(control_1_ld_ir), .EN_IR(control_1_en_ir), .CLK_N(not_1_out),
    .ADDR_OUT({ir_1_addr_out[3], WBUS[2:0]}), .OPCODE(OPCODE));
  // Probe on WBUS
endmodule

module IR (
  input  [7:0] IR_IN,
  input  LD_IR,
  input  EN_IR,
  input  CLK_N,
  output [3:0] ADDR_OUT,
  output [3:0] OPCODE
);

  wire [3:0] register_1_q;
  wire [7:0] multiplexer_1_out;

  Multiplexer #(.width(8)) multiplexer_1 (
    .in0({OPCODE, register_1_q}), .in1(IR_IN), .out(multiplexer_1_out), .sel(LD_IR));
  Register #(.trigger("falling")) register_1 (
    .D(multiplexer_1_out), .Q({OPCODE, register_1_q}), .clk(CLK_N));  // open: en, clr
  assign ADDR_OUT = EN_IR ? register_1_q : 4'bz;  // Controlled_Buffer controlled_buffer_1
endmodule

module AR (
  input  [2:0] AR_IN,
  input  LD_AR,
  input  EN_AR,
  input  CLK_N,
  output [2:0] AR_OUT
);

  wire [2:0] multiplexer_1_out, register_1_q;

  Multiplexer #(.width(3)) multiplexer_1 (.in0(register_1_q), .in1(AR_IN), .out(multiplexer_1_out), .sel(LD_AR));
  Register #(.trigger("falling"), .width(3)) register_1 (
    .D(multiplexer_1_out), .Q(register_1_q), .clk(CLK_N));  // open: en, clr
  assign AR_OUT = EN_AR ? register_1_q : 3'bz;  // Controlled_Buffer controlled_buffer_1
endmodule

module PC (
  input  EN_PC,
  input  INC_PC,
  input  CLK,
  input  CLR,
  output [2:0] PC_OUT
);

  wire and_1_out;
  wire [2:0] counter_1_q;

  Counter #(.max('h7), .ongoal("stay"), .width(3)) counter_1 (
    .Q(counter_1_q), .clk(and_1_out), .clr(CLR));  // open: load, D, count, carry, up
  and and_1 (and_1_out, INC_PC, CLK);
  assign PC_OUT = EN_PC ? counter_1_q : 3'bz;  // Controlled_Buffer controlled_buffer_1
endmodule
