// Logisim project arch.circ as structural Verilog
module SAP1 (
  input  in_1,
  output [7:0] out_2
);

  wire CLK, clock_1_out, EN_ACC, EN_ALU, EN_IR, EN_PC, EN_RAM, EN_SUB, HLT, INC_PC, LD_ACC, LD_B, LD_IR,
       LD_MAR, LD_OUT, not_1_out;
  wire [3:0] ir_1_opcode_out, mar_1_mar_out, outreg_1_outreg_out, outreg_1_outreg_out_2;
  wire [7:0] acc_1_acc_alu_out, breg_1_breg_out, WBUS;

  CTRLSEQR ctrlseqr_1 (
    .CLK(CLK), .OPCODE_IN(ir_1_opcode_out), .CLR(in_1), .HLT(HLT), .EN_ALU(EN_ALU), .LD_B(LD_B),
    .LD_OUT(LD_OUT), .INC_PC(INC_PC), .EN_PC(EN_PC), .LD_MAR(LD_MAR), .EN_RAM(EN_RAM), .LD_IR(LD_IR),
    .EN_IR(EN_IR), .LD_ACC(LD_ACC), .EN_ACC(EN_ACC), .EN_SUB(EN_SUB));
  not not_1 (not_1_out, HLT);
  Clock clock_1 (.out(clock_1_out));
  MAR mar_1 (.ADDR(WBUS[3:0]), .LD_MAR(LD_MAR), .CLK(CLK), .MAR_OUT(mar_1_mar_out));
  and and_1 (CLK, not_1_out, clock_1_out);
  PC pc_1 (.INC_PC(INC_PC), .CLK(CLK), .CLR(in_1), .EN_PC(EN_PC), .PC_OUT(WBUS[3:0]));
  RAM16x8 ram16x8_1 (.EN_RAM(EN_RAM), .ADDR_IN(mar_1_mar_out), .RAM_OUT(WBUS));
  IR ir_1 (
    .INST_IN(WBUS), .LD_IR(LD_IR), .CLK(CLK), .CLR(in_1), .EN_IR(EN_IR), .ADDR_OUT(WBUS[3:0]),
    .OPCODE_OUT(ir_1_opcode_out));
  Counter counter_1 (.Q(out_2), .clk(CLK), .clr(in_1));  // open: load, D, count, carry, up
  // Probe on WBUS
  ACC acc_1 (
    .ACC_IN(WBUS), .LD_ACC(LD_ACC), .EN_ACC(EN_ACC), .CLK(CLK), .ACC_OUT(WBUS),
    .ACC_ALU_OUT(acc_1_acc_alu_out));
  ALU alu_1 (.EN_SUB(EN_SUB), .EN_ALU(EN_ALU), .ACC_IN(acc_1_acc_alu_out), .BREG_IN(breg_1_breg_out), .ALU_OUT(WBUS));
  Hex_Digit_Display hex_digit_display_1 (.value(outreg_1_outreg_out_2));  // open: dp
  Hex_Digit_Display hex_digit_display_2 (.value(outreg_1_outreg_out));  // open: dp
  BREG breg_1 (.LD_B(LD_B), .CLK(CLK), .BREG_IN(WBUS), .BREG_OUT(breg_1_breg_out));
  OUTREG outreg_1 (
    .LD_OUT(LD_OUT), .OUTREG_IN(WBUS), .CLK(CLK), .OUTREG_OUT({outreg_1_outreg_out_2, outreg_1_outreg_out}));

  // Other names for the same wires on the sheet: CLR = in_1
endmodule

module SAP1_VAR (
  input  in_1,
  output [7:0] out_2
);

  wire CLK, clock_1_out, EN_ACC, EN_ALU, EN_IR, EN_PC, EN_RAM, EN_SUB, HLT, INC_PC, LD_ACC, LD_B, LD_IR,
       LD_MAR, LD_OUT, not_1_out;
  wire [3:0] ir_1_opcode_out, mar_1_mar_out, outreg_1_outreg_out, outreg_1_outreg_out_2;
  wire [7:0] acc_1_acc_alu_out, breg_1_breg_out, WBUS;

  CTRLSEQR_VAR ctrlseqr_var_1 (
    .CLK(CLK), .CLR(in_1), .OPCODE_IN(ir_1_opcode_out), .HLT(HLT), .EN_ALU(EN_ALU), .LD_B(LD_B),
    .LD_OUT(LD_OUT), .INC_PC(INC_PC), .EN_PC(EN_PC), .LD_MAR(LD_MAR), .EN_RAM(EN_RAM), .LD_IR(LD_IR),
    .EN_IR(EN_IR), .LD_ACC(LD_ACC), .EN_ACC(EN_ACC), .EN_SUB(EN_SUB));
  not not_1 (not_1_out, HLT);
  Clock clock_1 (.out(clock_1_out));
  MAR mar_1 (.ADDR(WBUS[3:0]), .LD_MAR(LD_MAR), .CLK(CLK), .MAR_OUT(mar_1_mar_out));
  and and_1 (CLK, not_1_out, clock_1_out);
  PC pc_1 (.INC_PC(INC_PC), .CLK(CLK), .CLR(in_1), .EN_PC(EN_PC), .PC_OUT(WBUS[3:0]));
  RAM16x8 ram16x8_1 (.EN_RAM(EN_RAM), .ADDR_IN(mar_1_mar_out), .RAM_OUT(WBUS));
  IR ir_1 (
    .INST_IN(WBUS), .LD_IR(LD_IR), .CLK(CLK), .CLR(in_1), .EN_IR(EN_IR), .ADDR_OUT(WBUS[3:0]),
    .OPCODE_OUT(ir_1_opcode_out));
  Counter counter_1 (.Q(out_2), .clk(CLK), .clr(in_1));  // open: load, D, count, carry, up
  // Probe on WBUS
  ACC acc_1 (
    .ACC_IN(WBUS), .LD_ACC(LD_ACC), .EN_ACC(EN_ACC), .CLK(CLK), .ACC_OUT(WBUS),
    .ACC_ALU_OUT(acc_1_acc_alu_out));
  ALU alu_1 (.EN_SUB(EN_SUB), .EN_ALU(EN_ALU), .ACC_IN(acc_1_acc_alu_out), .BREG_IN(breg_1_breg_out), .ALU_OUT(WBUS));
  Hex_Digit_Display hex_digit_display_1 (.value(outreg_1_outreg_out_2));  // open: dp
  Hex_Digit_Display hex_digit_display_2 (.value(outreg_1_outreg_out));  // open: dp
  BREG breg_1 (.LD_B(LD_B), .CLK(CLK), .BREG_IN(WBUS), .BREG_OUT(breg_1_breg_out));
  OUTREG outreg_1 (
    .LD_OUT(LD_OUT), .OUTREG_IN(WBUS), .CLK(CLK), .OUTREG_OUT({outreg_1_outreg_out_2, outreg_1_outreg_out}));

  // Other names for the same wires on the sheet: CLR = in_1
endmodule

module PC (
  input  INC_PC,
  input  CLK,
  input  CLR,
  input  EN_PC,
  output [3:0] PC_OUT
);

  wire not_1_out;
  wire [3:0] counter_1_q;

  not not_1 (not_1_out, INC_PC);
  Counter #(.max('hf), .width(4)) counter_1 (
    .load(not_1_out), .D(counter_1_q), .Q(counter_1_q), .clk(CLK), .clr(CLR));  // open: count, carry, up
  assign PC_OUT = EN_PC ? counter_1_q : 4'bz;  // Controlled_Buffer controlled_buffer_1
endmodule

module MAR (
  input  [3:0] ADDR,
  input  LD_MAR,
  input  CLK,
  output [3:0] MAR_OUT
);

  wire [3:0] multiplexer_1_out;

  Multiplexer #(.width(4)) multiplexer_1 (.in0(MAR_OUT), .in1(ADDR), .out(multiplexer_1_out), .sel(LD_MAR));
  Register #(.width(4)) register_1 (.D(multiplexer_1_out), .Q(MAR_OUT), .clk(CLK));  // open: en, clr
endmodule

module RAM16x8 (
  input  [3:0] ADDR_IN,
  input  EN_RAM,
  output [7:0] RAM_OUT
);

  wire [7:0] ram_1_dout;

  RAM #(.addrWidth(4), .enables("line")) ram_1 (.addr(ADDR_IN), .dout(ram_1_dout));  // open: we, clk, din
  assign RAM_OUT = EN_RAM ? ram_1_dout : 8'bz;  // Controlled_Buffer controlled_buffer_1
endmodule

module IR (
  input  [7:0] INST_IN,
  input  LD_IR,
  input  CLK,
  input  CLR,
  input  EN_IR,
  output [3:0] ADDR_OUT,
  output [3:0] OPCODE_OUT
);

  wire [3:0] register_1_q;
  wire [7:0] multiplexer_1_out;

  Multiplexer #(.width(8)) multiplexer_1 (
    .in0({OPCODE_OUT, register_1_q}), .in1(INST_IN), .out(multiplexer_1_out), .sel(LD_IR));
  Register register_1 (.D(multiplexer_1_out), .Q({OPCODE_OUT, register_1_q}), .clk(CLK), .clr(CLR));  // open: en
  assign ADDR_OUT = EN_IR ? register_1_q : 4'bz;  // Controlled_Buffer controlled_buffer_1
endmodule

module CTRLSEQR (
  input  [3:0] OPCODE_IN,
  input  CLK,
  input  CLR,
  output HLT,
  output INC_PC,
  output EN_PC,
  output LD_MAR,
  output EN_RAM,
  output LD_IR,
  output EN_IR,
  output LD_ACC,
  output EN_ACC,
  output EN_SUB,
  output EN_ALU,
  output LD_B,
  output LD_OUT
);

  wire and_1_out, and_3_out, and_4_out, and_5_out, and_6_out, and_7_out, and_8_out, and_10_out, and_11_out,
       and_12_out, decoder_1_out4, decoder_1_out5, decoder_1_out6, not_1_out, not_2_out, not_3_out,
       not_4_out, not_5_out, not_6_out, not_7_out, not_8_out, not_9_out, not_10_out, not_11_out, not_12_out,
       not_13_out, not_14_out, not_15_out, or_1_out, or_2_out;
  wire [2:0] counter_1_q;

  not not_1 (not_1_out, CLR);
  and and_1 (and_1_out, not_1_out, decoder_1_out6);
  Counter #(.max('h6), .trigger("falling"), .width(3)) counter_1 (
    .load(and_1_out), .D(3'b001), .Q(counter_1_q), .clk(CLK), .clr(CLR));  // open: count, carry, up
  Decoder #(.select(3)) decoder_1 (
    .out1(EN_PC), .out2(INC_PC), .out3(LD_IR), .out4(decoder_1_out4), .out5(decoder_1_out5),
    .out6(decoder_1_out6), .sel(counter_1_q));  // open: out0, out7, en
  not not_2 (not_2_out, OPCODE_IN[2]);
  not not_3 (not_3_out, OPCODE_IN[3]);
  and and_2 (HLT, OPCODE_IN[0], OPCODE_IN[1], OPCODE_IN[2], OPCODE_IN[3], decoder_1_out6);
  and and_3 (and_3_out, not_2_out, not_3_out);
  not not_4 (not_4_out, OPCODE_IN[3]);
  not not_5 (not_5_out, OPCODE_IN[2]);
  and and_4 (and_4_out, decoder_1_out5, not_4_out, not_5_out, not_6_out, not_7_out);
  not not_6 (not_6_out, OPCODE_IN[1]);
  not not_7 (not_7_out, OPCODE_IN[0]);
  or or_1 (or_1_out, OPCODE_IN[0], OPCODE_IN[1]);
  and and_5 (and_5_out, decoder_1_out6, or_1_out, not_8_out, not_9_out);
  not not_8 (not_8_out, OPCODE_IN[3]);
  not not_9 (not_9_out, OPCODE_IN[2]);
  and and_6 (and_6_out, OPCODE_IN[3], OPCODE_IN[2], OPCODE_IN[1], not_10_out);
  not not_10 (not_10_out, OPCODE_IN[0]);
  not not_11 (not_11_out, OPCODE_IN[3]);
  not not_12 (not_12_out, OPCODE_IN[2]);
  not not_13 (not_13_out, OPCODE_IN[0]);
  not not_14 (not_14_out, OPCODE_IN[3]);
  not not_15 (not_15_out, OPCODE_IN[2]);
  and and_7 (and_7_out, decoder_1_out4, and_3_out);
  and and_8 (and_8_out, and_3_out, decoder_1_out5);
  and and_9 (EN_ACC, decoder_1_out4, and_6_out);
  and and_10 (and_10_out, not_11_out, not_12_out, OPCODE_IN[1], not_13_out);
  or or_2 (or_2_out, OPCODE_IN[0], OPCODE_IN[1]);
  and and_11 (and_11_out, or_2_out, and_12_out);
  and and_12 (and_12_out, not_14_out, not_15_out);
  or or_3 (LD_MAR, EN_PC, and_7_out);
  or or_4 (EN_RAM, LD_IR, and_8_out);
  and and_13 (EN_IR, decoder_1_out4, and_3_out);
  or or_5 (LD_ACC, and_4_out, and_5_out);
  and and_14 (EN_SUB, decoder_1_out6, and_10_out);
  and and_15 (EN_ALU, decoder_1_out6, and_11_out);
  and and_16 (LD_B, decoder_1_out5, and_11_out);
  and and_17 (LD_OUT, and_6_out, decoder_1_out4);
endmodule

module CTRLSEQR_VAR (
  input  [3:0] OPCODE_IN,
  input  CLK,
  input  CLR,
  output HLT,
  output INC_PC,
  output EN_PC,
  output LD_MAR,
  output EN_RAM,
  output LD_IR,
  output EN_IR,
  output LD_ACC,
  output EN_ACC,
  output EN_SUB,
  output EN_ALU,
  output LD_B,
  output LD_OUT
);

  wire and_1_out, and_3_out, and_4_out, and_5_out, and_6_out, and_7_out, and_8_out, and_10_out, and_11_out,
       and_12_out, comparator_1_eq, not_1_out, not_2_out, not_3_out, not_4_out, not_5_out, not_6_out,
       not_7_out, not_8_out, not_9_out, not_10_out, not_11_out, not_12_out, not_13_out, not_14_out,
       not_15_out, or_1_out, or_2_out, or_3_out;
  wire [2:0] counter_1_q;
  wire [5:0] rom_1_data;
  wire [5:3] decoder_1_out4;

  not not_1 (not_1_out, CLR);
  and and_1 (and_1_out, not_1_out, decoder_1_out4[5]);
  or or_1 (or_1_out, comparator_1_eq, and_1_out);
  Counter #(.max('h6), .trigger("falling"), .width(3)) counter_1 (
    .load(or_1_out), .D(3'b001), .Q(counter_1_q), .clk(CLK), .clr(CLR));  // open: count, carry, up
  Decoder #(.select(3)) decoder_1 (
    .out1(EN_PC), .out2(INC_PC), .out3(LD_IR), .out4(decoder_1_out4[3]), .out5(decoder_1_out4[4]),
    .out6(decoder_1_out4[5]), .sel(counter_1_q));  // open: out0, out7, en
  not not_2 (not_2_out, OPCODE_IN[2]);
  not not_3 (not_3_out, OPCODE_IN[3]);
  ROM #(.addrWidth(4), .dataWidth(6)) rom_1 (.addr(OPCODE_IN), .data(rom_1_data));
  and and_2 (HLT, OPCODE_IN[0], OPCODE_IN[1], OPCODE_IN[2], OPCODE_IN[3], decoder_1_out4[3]);
  and and_3 (and_3_out, not_2_out, not_3_out);
  not not_4 (not_4_out, OPCODE_IN[3]);
  not not_5 (not_5_out, OPCODE_IN[2]);
  and and_4 (and_4_out, decoder_1_out4[4], not_4_out, not_5_out, not_6_out, not_7_out);
  not not_6 (not_6_out, OPCODE_IN[1]);
  not not_7 (not_7_out, OPCODE_IN[0]);
  or or_2 (or_2_out, OPCODE_IN[0], OPCODE_IN[1]);
  and and_5 (and_5_out, decoder_1_out4[5], or_2_out, not_8_out, not_9_out);
  not not_8 (not_8_out, OPCODE_IN[3]);
  not not_9 (not_9_out, OPCODE_IN[2]);
  and and_6 (and_6_out, OPCODE_IN[3], OPCODE_IN[2], OPCODE_IN[1], not_10_out);
  not not_10 (not_10_out, OPCODE_IN[0]);
  not not_11 (not_11_out, OPCODE_IN[3]);
  not not_12 (not_12_out, OPCODE_IN[2]);
  not not_13 (not_13_out, OPCODE_IN[0]);
  not not_14 (not_14_out, OPCODE_IN[3]);
  not not_15 (not_15_out, OPCODE_IN[2]);
  and and_7 (and_7_out, decoder_1_out4[3], and_3_out);
  and and_8 (and_8_out, and_3_out, decoder_1_out4[4]);
  and and_9 (EN_ACC, decoder_1_out4[3], and_6_out);
  and and_10 (and_10_out, not_11_out, not_12_out, OPCODE_IN[1], not_13_out);
  or or_3 (or_3_out, OPCODE_IN[0], OPCODE_IN[1]);
  and and_11 (and_11_out, or_3_out, and_12_out);
  and and_12 (and_12_out, not_14_out, not_15_out);
  or or_4 (LD_MAR, EN_PC, and_7_out);
  or or_5 (EN_RAM, LD_IR, and_8_out);
  and and_13 (EN_IR, decoder_1_out4[3], and_3_out);
  or or_6 (LD_ACC, and_4_out, and_5_out);
  and and_14 (EN_SUB, decoder_1_out4[5], and_10_out);
  and and_15 (EN_ALU, decoder_1_out4[5], and_11_out);
  and and_16 (LD_B, decoder_1_out4[4], and_11_out);
  and and_17 (LD_OUT, and_6_out, decoder_1_out4[3]);
  Comparator #(.width(6)) comparator_1 (
    .a({decoder_1_out4, LD_IR, INC_PC, EN_PC}), .b(rom_1_data), .eq(comparator_1_eq));  // open: gt, lt

  // Notes on the sheet:
  //   contents of rom_1 (hex, n*v repeats v):
  //   10 13*0 8 5
endmodule

module ACC (
  input  [7:0] ACC_IN,
  input  LD_ACC,
  input  EN_ACC,
  input  CLK,
  output [7:0] ACC_OUT,
  output [7:0] ACC_ALU_OUT
);

  wire [7:0] multiplexer_1_out;

  Multiplexer #(.width(8)) multiplexer_1 (.in0(ACC_ALU_OUT), .in1(ACC_IN), .out(multiplexer_1_out), .sel(LD_ACC));
  Register register_1 (.D(multiplexer_1_out), .Q(ACC_ALU_OUT), .clk(CLK));  // open: en, clr
  assign ACC_OUT = EN_ACC ? ACC_ALU_OUT : 8'bz;  // Controlled_Buffer controlled_buffer_1
endmodule

module OUTREG (
  input  LD_OUT,
  input  [7:0] OUTREG_IN,
  input  CLK,
  output [7:0] OUTREG_OUT
);

  Register register_1 (.D(OUTREG_IN), .en(LD_OUT), .Q(OUTREG_OUT), .clk(CLK));  // open: clr
endmodule

module BREG (
  input  LD_B,
  input  CLK,
  input  [7:0] BREG_IN,
  output [7:0] BREG_OUT
);

  OUTREG outreg_1 (.LD_OUT(LD_B), .OUTREG_IN(BREG_IN), .CLK(CLK), .OUTREG_OUT(BREG_OUT));
endmodule

module ALU (
  input  EN_ALU,
  input  [7:0] ACC_IN,
  input  [7:0] BREG_IN,
  input  EN_SUB,
  output [7:0] ALU_OUT
);

  wire [7:0] adder_1_out, multiplexer_1_out, subtractor_1_out;

  Adder adder_1 (.a(ACC_IN), .b(BREG_IN), .out(adder_1_out));  // open: cin, cout
  Subtractor subtractor_1 (.a(ACC_IN), .b(BREG_IN), .out(subtractor_1_out));  // open: bin, bout
  Multiplexer #(.width(8)) multiplexer_1 (
    .in0(adder_1_out), .in1(subtractor_1_out), .out(multiplexer_1_out), .sel(EN_SUB));
  assign ALU_OUT = EN_ALU ? multiplexer_1_out : 8'bz;  // Controlled_Buffer controlled_buffer_1
endmodule
